# Fritzing sketch ACS712 ile AkımÖlçer (saved by Fritzing 0.9.0b)
breadboards: 1

parts:
  Eleman1 = Arduino Uno (Rev3)
  Eleman2 = ACS712 Low Current Sensor Board v12
  LCD1 = LCD screen
  R2 = Rotary Potentiometer (Large) [maximum_resistance=100kΩ package=THT]
  BAT1 = BC9VPC [package=bc9vpc]

nets:
  N1: Eleman1.A0, Eleman2.VO
  N2: Eleman1.D11_PWM/MOSI, LCD1.E
  N3: Eleman1.D12/MISO, LCD1.RS
  GND: Eleman1.GND, Eleman2.GND, LCD1.VSS, LCD1.R/W, LCD1.LED-, R2.leg1
  N4: Eleman1.D2, LCD1.DB7
  N5: Eleman1.D3_PWM, LCD1.DB6
  N6: Eleman1.D4, LCD1.DB5
  N7: Eleman1.D5_PWM, LCD1.DB4
  5V: Eleman1.5V, Eleman2.5V, LCD1.VDD, LCD1.LED+, R2.leg2
  N8: Eleman2.IP+, BAT1.V+, BAT1.V-
  N9: LCD1.V0, R2.wiper
